# Fritzing sketch 2020-02-20- Mod Simon (saved by Fritzing 0.9.3b)
circuit board: 8.46667cm x 5.64444cm
breadboards: 1

parts:
  Bauteil1 = Arduino Nano (Rev3.0) (ICSP)
  LED1 = LED - 5mm [color="Red (633nm)" package="5 mm [THT]"]
  LED2 = LED - 5mm [color="Yellow (595nm)" package="5 mm [THT]"]
  LED3 = LED - 5mm [color="Green (570nm)" package="5 mm [THT]"]
  R1 = Resistor [tolerance=±5% resistance=150 package=THT]
  R2 = Resistor [tolerance=±5% resistance=150 package=THT]
  R3 = Resistor [tolerance=±5% resistance=150 package=THT]
  S1 = Pushbutton [package="[THT]"]
  S2 = Pushbutton [package="[THT]"]
  S3 = Pushbutton [package="[THT]"]
  R4 = Resistor [tolerance=±5% resistance=10k package=THT]
  R7 = Resistor [tolerance=±5% resistance=10k package=THT]
  R8 = Resistor [tolerance=±5% resistance=10k package=THT]
  BAT1 = BC9VPC [package=bc9vpc]
  S4 = Pushbutton [package="[THT]"]
  R9 = Resistor [tolerance=±5% resistance=10k package=THT]
  LED4 = LED - 5mm [color="Blue (525nm)" package="5 mm [THT]"]
  R10 = Resistor [tolerance=±5% resistance=100 package=THT]

nets:
  N1: Bauteil1.GND, R1.Pin_0, R2.Pin_0, R3.Pin_0, R4.Pin_0, R7.Pin_0, R8.Pin_0, BAT1.V-, R9.Pin_0, R10.Pin_0
  N2: Bauteil1.D5, LED4.cathode
  N3: Bauteil1.D6, LED1.cathode
  N4: Bauteil1.D7, LED2.cathode
  N5: Bauteil1.D8, LED3.cathode
  N6: Bauteil1.VIN, BAT1.V+
  N7: Bauteil1.5V, S1.Pin_3, S1.Pin_4, S2.Pin_3, S2.Pin_4, S3.Pin_3, S3.Pin_4, S4.Pin_3, S4.Pin_4
  N8: Bauteil1.A7, S1.Pin_1, S1.Pin_2, R4.Pin_1
  N9: Bauteil1.A6, S2.Pin_1, S2.Pin_2, R7.Pin_1
  N10: Bauteil1.A5, S3.Pin_1, S3.Pin_2, R8.Pin_1
  N11: Bauteil1.A4, S4.Pin_1, S4.Pin_2, R9.Pin_1
  N12: LED1.anode, R1.Pin_1
  N13: LED2.anode, R2.Pin_1
  N14: LED3.anode, R3.Pin_1
  N15: LED4.anode, R10.Pin_1

// code stored in the sketch: 2020-02-06-erstesArduinoProgramm.ino
int Taster1 = 20; // Taster "Start Band1" am Pin2
int Taster2 = 21; // Taster "Start Band2" am Pin3
int Taster3 = 22; // Taster "Start Band3" am Pin4

int LEDrot = 9;
int LEDgelb = 10;
int LEDgruen = 11;

void setup() //Hier beginnt das Setup.

{
  // Eingaenge der Taster:
  
  pinMode(20, INPUT);
  pinMode(21, INPUT);
  pinMode(22, INPUT);
  

  //Ausgaenge der LEDs:
  
  pinMode(9,OUTPUT);
  pinMode(10,OUTPUT);
  pinMode(11,OUTPUT);
  
  
  // Alle LEDs aus:

  digitalWrite (LEDrot,LOW);
  digitalWrite (LEDgelb,LOW);
  digitalWrite (LEDgruen,LOW);
}


void loop()

{

  // ===================
  // Programmabschnitt 1
  // ===================
  
  {
    if ((digitalRead(Taster1) == HIGH) && (digitalRead(LEDrot) == LOW))
    {
      digitalWrite(LEDrot,HIGH); // rote LED ein
      delay(5); // Durch diese Pause bleibt die LED eine Sekunde aus.
    }
    else
    {
      digitalWrite(LEDrot, LOW);
      delay(5);
    }
  }
  
 
 {
    if ((digitalRead(Taster2) == HIGH) && (digitalRead(LEDgelb) == LOW))
    {
      digitalWrite(LEDgelb,HIGH); // gelbe LED ein
      delay(5); // Durch diese Pause bleibt die LED eine Sekunde aus.
    }
    else
    {
      digitalWrite(LEDgelb, LOW);
      delay(5);
    }
   }

 {
    if ((digitalRead(Taster3) == HIGH) && (digitalRead(LEDgruen) == LOW))
    {
      digitalWrite(LEDgruen,HIGH); // gruene LED ein
      delay(5); // Durch diese Pause bleibt die LED eine Sekunde aus.
    }
    else
    {
      digitalWrite(LEDgruen, LOW);
      delay(5);
    }
 }
 
}
